# Fritzing sketch electronics (saved by Fritzing 0.9.3b)
circuit board: 8.46667cm x 5.64444cm
breadboards: 1

parts:
  co2 = male pin header, 3 pins [form="♂ (male)"]
  pH_Circuit2 = pH Circuit
  Mixer = DC Motor
  flour_servo = male pin header, 3 pins [form="♂ (male)"]
  12V1 = Power plug
  C1 = Electrolytic Capacitor [capacitance=10µF voltage=50V package="100 mil [THT, electrolytic]"]
  R1 = Resistor [tolerance=±5% resistance=10k package=THT]
  Part3 = Photon
  H-bridge1 = L293D [package=THT]
  C2 = Electrolytic Capacitor [capacitance=10µF voltage=50V package="100 mil [THT, electrolytic]"]
  IC3 = Voltage Regulator [package=78xxl]
  Pump = DC Motor
  R2 = Resistor [tolerance=±5% resistance=20k package=THT]
  Pre-Assembled_Female_BNC1 = Pre-Assembled Female BNC

nets:
  N1: co2.pin1, R1.Pin_0
  N2: co2.pin2, flour_servo.pin2, Part3.VIN, H-bridge1.+V, C2.+, IC3.OUT
  GND: co2.pin3, pH_Circuit2.GND#0, flour_servo.pin3, 12V1.GND, C1.-, Part3.GND, H-bridge1.0V, C2.-, IC3.GND, R2.Pin_1
  N3: pH_Circuit2.RX, Part3.TX
  VCC: pH_Circuit2.Vcc, Part3.3V3, Pre-Assembled_Female_BNC1.NC
  N4: pH_Circuit2.PRB, Pre-Assembled_Female_BNC1.PRB
  N5: pH_Circuit2.GND#5, Pre-Assembled_Female_BNC1.GND
  N6: Mixer.pin_1, H-bridge1.Out_4_(_Controlled_by_Enable_2_)
  N7: Mixer.pin_2, H-bridge1.Out_3_(_Controlled_by_Enable_2_)
  N8: flour_servo.pin1, Part3.D2
  N9: 12V1.VCC, C1.+, H-bridge1.+Vmotor, IC3.IN
  N10: R1.Pin_1, Part3.A4, R2.Pin_0
  N11: Part3.A0, H-bridge1.In_4
  N12: Part3.A1, H-bridge1.In_3
  N13: Part3.A2, H-bridge1.In_1
  N14: Part3.A3, H-bridge1.In_2
  N15: Part3.D0, H-bridge1.Enable_2
  N16: Part3.D1, H-bridge1.Enable_1
  N17: H-bridge1.Out_1_(_Controlled_by_Enable_1_), Pump.pin_2
  N18: H-bridge1.Out_2_(_Controlled_by_Enable_1_), Pump.pin_1
